# Fritzing sketch ArduinoHueCTSensor_circuit (saved by Fritzing 0.9.3b)
breadboards: 1

parts:
  Part2 = Arduino MKR1000
  Part3 = Adafruit TCS34725 RGB Color Sensor [part_number="Adafruit #1334"]
  Part4 = OLED Monochrome 128x32 I2C [part_number=931]

nets:
  3.3V: Part2.VCC, Part3.VIN, Part4.VIN
  GND: Part2.GND, Part3.GND, Part3.LED_EN, Part4.GND
  N1: Part2.D12_SCL, Part3.SDA, Part4.SDA
  N2: Part2.D13_RX, Part3.SCL, Part4.SCL

custom parts:
  Arduino MKR1000: MKR1000 is a powerful board that combines the functionality of the Zero and the Wi-Fi Shield. It is the ideal solution for makers wanting to design IoT projects with minimal previous experience in networking
  Adafruit TCS34725 RGB Color Sensor: Your electronics can now see in dazzling color with this lovely color light sensor. We found the best color sensor on the market, the TCS34725, which has RGB and Clear light sensing elements. An IR blocking filter, integrated on-chip and localized to the color sensing photodiodes, minimizes the IR spectral component of the incoming light and allows color measurements to be made accurately. The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
  OLED Monochrome 128x32 I2C: These displays are small, only about 1" diagonal, but very readable due to the high contrast of an OLED display. This display is made of 128x32 individual white OLED pixels, each one is turned on or off by the controller chip. Because the display makes its own light, no backlight is required. This reduces the power required to run the OLED and is why the display has such high contrast; we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
